# Fritzing sketch KAneda-JFG (saved by Fritzing 1.0.1rc)

parts:
  Acelerómetro_MPU-6050 = InvenSense MPU6050
  IC1 = Rasberry Pi NIOR Camera [chip_label=IC package="DIP (Dual Inline) [THT]"]  # not connected
  U1 = Battery Holders [package=lipo-1100mAh]
  Raspberry_Pi1 = Raspberry Pi Zero
  GM15BY3 = Micromotor Stepper GM15BY 15mm
  M1 = DC Motor [voltage_(max)=6V voltage_(min)=3V]
  VCC1 = Battery block 9V
  X1 = USB Connectors [package=usb-microb]
  J1 = Basic Servo
  M2 = BTS7960
  Componente1 = Power Cell LiPo Charger/Booster

nets:
  VCC: Acelerómetro_MPU-6050.VCC, Raspberry_Pi1.3v3
  GND: Acelerómetro_MPU-6050.GND, Raspberry_Pi1.GND, J1.gnd, M2.pin8
  N1: Acelerómetro_MPU-6050.SCL, Raspberry_Pi1.GPIO3
  N2: Acelerómetro_MPU-6050.SDA, Raspberry_Pi1.GPIO2
  N3: U1.+, Componente1.VCC
  GND_2: U1.-, X1.GND, Componente1.GND
  N4: Raspberry_Pi1.GIPO9, J1.pulse
  N5: Raspberry_Pi1.GIPO6, GM15BY3.C
  N6: Raspberry_Pi1.GIPO13, M2.pin1
  N7: Raspberry_Pi1.GIPO19, GM15BY3.B
  N8: Raspberry_Pi1.GIPO12, M2.pin2
  N9: Raspberry_Pi1.GIPO15, M2.pin3, M2.pin5
  N10: Raspberry_Pi1.GIPO14, M2.pin4, M2.pin6
  5V: Raspberry_Pi1.5V, J1.vcc, M2.pin7
  N11: Raspberry_Pi1.PWR_IN, X1.D+, X1.D-
  N12: GM15BY3.A, VCC1.+, M2.pin11
  N13: GM15BY3.D, VCC1.-, M2.pin12
  N14: M1.pin_1, M2.pin9
  N15: M1.pin_2, M2.pin10
  N16: X1.VBUS, Componente1.5VIN

custom parts:
  Rasberry Pi NIOR Camera: Camera
  Raspberry Pi Zero: The Raspberry Pi Zero is the latest single board computer to be released by the Raspberry Pi Foundation. It is the entry level model Raspberry Pi perfect for hobbyists, makers and industrial engineers looking to create solutions where small size and low power consumption are important. This is especially relevant for applications in the wearables space as well as up and coming applications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
  Micromotor Stepper GM15BY 15mm: Motor paso a paso de 5V ultra pequeño con reductora de 1:150.
  BTS7960: BTS7960 43A Peak Power H-Bridge PWM Motor Driver
